// Logisim project circuits.circ as structural Verilog
module half_adder (
  input  in_1,
  input  in_2,
  output out_3,
  output out_4
);

  and and_1 (out_4, in_1, in_2);
  xor xor_1 (out_3, in_1, in_2);
endmodule

module full_adder_usingHalg (
  input  A,
  input  B,
  input  Cin,
  output sum,
  output carry
);

  wire half_adder_1_out_3, half_adder_1_out_4, half_adder_2_out_4;

  half_adder half_adder_1 (.in_1(A), .in_2(B), .out_3(half_adder_1_out_3), .out_4(half_adder_1_out_4));
  half_adder half_adder_2 (.in_1(half_adder_1_out_3), .in_2(Cin), .out_3(sum), .out_4(half_adder_2_out_4));
  or or_1 (carry, half_adder_2_out_4, half_adder_1_out_4);
endmodule

module full_adder (
  input  A,
  input  B,
  input  cin,
  output s,
  output c
);

  wire and_1_out, and_2_out, xor_1_out;

  xor xor_1 (xor_1_out, A, B);
  xor xor_2 (s, xor_1_out, cin);
  and and_1 (and_1_out, cin, xor_1_out);
  and and_2 (and_2_out, A, B);
  or or_1 (c, and_1_out, and_2_out);
endmodule

module binary_adder (
  input  Cin,
  input  A1,
  input  B1,
  input  A2,
  input  B2,
  input  A3,
  input  B3,
  input  A4,
  input  B4,
  output s1,
  output s2,
  output s3,
  output s4,
  output Cout
);

  wire full_adder_usinghalg_1_carry, full_adder_usinghalg_2_carry, full_adder_usinghalg_3_carry;

  full_adder_usingHalg full_adder_usinghalg_1 (
    .A(A1), .B(B1), .Cin(Cin), .sum(s1), .carry(full_adder_usinghalg_1_carry));
  full_adder_usingHalg full_adder_usinghalg_2 (
    .A(A2), .B(B2), .Cin(full_adder_usinghalg_1_carry), .sum(s2), .carry(full_adder_usinghalg_2_carry));
  full_adder_usingHalg full_adder_usinghalg_3 (
    .A(A3), .B(B3), .Cin(full_adder_usinghalg_2_carry), .sum(s3), .carry(full_adder_usinghalg_3_carry));
  full_adder_usingHalg full_adder_usinghalg_4 (
    .A(A4), .B(B4), .Cin(full_adder_usinghalg_3_carry), .sum(s4), .carry(Cout));
endmodule

module halg_subtractor (
  input  B,
  input  A,
  output D,
  output Bow
);

  wire not_1_out;

  not not_1 (not_1_out, A);
  xor xor_1 (D, A, B);
  and and_1 (Bow, not_1_out, B);
endmodule

module full_subtractor (
  input  Bin,
  input  A,
  input  B,
  output D,
  output Bout
);

  wire halg_subtractor_1_bow, halg_subtractor_1_d, halg_subtractor_2_bow;

  halg_subtractor halg_subtractor_1 (.D(halg_subtractor_1_d), .Bow(halg_subtractor_1_bow), .B(A), .A(B));
  halg_subtractor halg_subtractor_2 (.D(D), .Bow(halg_subtractor_2_bow), .B(Bin), .A(halg_subtractor_1_d));
  or or_1 (Bout, halg_subtractor_2_bow, halg_subtractor_1_bow);
endmodule

module _4_bit_subtractor_adder (
  input  Cin,
  input  A1,
  input  B1,
  input  A2,
  input  B2,
  input  A3,
  input  B3,
  input  A4,
  input  B4,
  output s1,
  output s2,
  output s3,
  output s4,
  output Cout
);

  wire full_adder_usinghalg_1_carry, full_adder_usinghalg_2_carry, full_adder_usinghalg_3_carry, xor_1_out,
       xor_2_out, xor_3_out, xor_4_out;

  xor xor_1 (xor_1_out, Cin, B1);
  xor xor_2 (xor_2_out, Cin, B2);
  xor xor_3 (xor_3_out, Cin, B3);
  xor xor_4 (xor_4_out, Cin, B4);
  full_adder_usingHalg full_adder_usinghalg_1 (
    .A(A1), .B(xor_1_out), .Cin(Cin), .sum(s1), .carry(full_adder_usinghalg_1_carry));
  full_adder_usingHalg full_adder_usinghalg_2 (
    .A(A2), .B(xor_2_out), .Cin(full_adder_usinghalg_1_carry), .sum(s2), .carry(full_adder_usinghalg_2_carry));
  full_adder_usingHalg full_adder_usinghalg_3 (
    .A(A3), .B(xor_3_out), .Cin(full_adder_usinghalg_2_carry), .sum(s3), .carry(full_adder_usinghalg_3_carry));
  full_adder_usingHalg full_adder_usinghalg_4 (
    .A(A4), .B(xor_4_out), .Cin(full_adder_usinghalg_3_carry), .sum(s4), .carry(Cout));
endmodule

module _4_bit_mux (
  input  in_1,
  input  in_2,
  input  in_3,
  input  in_4,
  input  in_5,
  input  in_6,
  output out_7
);

  wire multiplexer_1_out, multiplexer_2_out;

  Multiplexer multiplexer_1 (.in0(in_1), .in1(in_2), .out(multiplexer_1_out), .sel(in_5));  // open: en
  Multiplexer multiplexer_2 (.in0(in_3), .in1(in_4), .out(multiplexer_2_out), .sel(in_5));  // open: en
  Multiplexer multiplexer_3 (.in0(multiplexer_1_out), .in1(multiplexer_2_out), .out(out_7), .sel(in_6));  // open: en
endmodule

module _1_bit_Alu (
  input  A,
  input  B,
  input  S1,
  input  S2,
  input  Cin,
  output out_6,
  output Cout
);

  wire and_1_out, full_adder_1_s, or_1_out, xor_1_out;

  and and_1 (and_1_out, A, B);
  or or_1 (or_1_out, A, B);
  xor xor_1 (xor_1_out, A, B);
  full_adder full_adder_1 (.A(A), .B(B), .cin(Cin), .s(full_adder_1_s), .c(Cout));
  _4_bit_mux u_4_bit_mux_1 (
    .in_1(and_1_out), .in_2(or_1_out), .in_3(xor_1_out), .in_4(full_adder_1_s), .in_5(S2), .in_6(S1),
    .out_7(out_6));
endmodule

module _4_bit_Alu (
  input  in_1,
  input  in_2,
  input  in_3,
  input  in_4,
  input  in_5,
  input  in_6,
  input  in_7,
  input  in_8,
  input  in_9,
  input  in_10,
  input  in_11,
  output out_12,
  output out_13,
  output out_14,
  output out_15,
  output out_16
);

  wire n1_bit_alu_1_cout, n1_bit_alu_2_cout, n1_bit_alu_3_cout;

  _1_bit_Alu u_1_bit_alu_1 (
    .A(in_4), .B(in_5), .Cin(in_3), .out_6(out_12), .S1(in_1), .S2(in_2), .Cout(n1_bit_alu_1_cout));
  _1_bit_Alu u_1_bit_alu_2 (
    .A(in_6), .B(in_7), .Cin(n1_bit_alu_1_cout), .out_6(out_13), .S1(in_1), .S2(in_2),
    .Cout(n1_bit_alu_2_cout));
  _1_bit_Alu u_1_bit_alu_3 (
    .A(in_8), .B(in_9), .Cin(n1_bit_alu_2_cout), .out_6(out_14), .S1(in_1), .S2(in_2),
    .Cout(n1_bit_alu_3_cout));
  _1_bit_Alu u_1_bit_alu_4 (
    .A(in_10), .B(in_11), .Cin(n1_bit_alu_3_cout), .out_6(out_15), .S1(in_1), .S2(in_2), .Cout(out_16));
endmodule

module Alu_1bit_logic (
  input  [3:0] Selector,
  input  A1,
  input  B1,
  output out_4
);

  wire and_1_out, and_2_out, nand_1_out, nor_1_out, not_1_out, not_2_out, not_3_out, not_4_out, not_5_out,
       not_6_out, or_1_out, or_2_out, or_3_out, xnor_1_out, xor_1_out;

  and and_1 (and_1_out, A1, B1);
  not not_1 (not_1_out, B1);
  not not_2 (not_2_out, B1);
  not not_3 (not_3_out, A1);
  not not_4 (not_4_out, B1);
  not not_5 (not_5_out, A1);
  nand nand_1 (nand_1_out, A1, B1);
  nor nor_1 (nor_1_out, A1, B1);
  not not_6 (not_6_out, and_1_out);
  xor xor_1 (xor_1_out, A1, B1);
  and and_2 (and_2_out, not_2_out, A1);
  or or_1 (or_1_out, not_3_out, B1);
  xnor xnor_1 (xnor_1_out, A1, B1);
  or or_2 (or_2_out, A1, B1);
  or or_3 (or_3_out, A1, not_4_out);
  Multiplexer #(.select(4)) multiplexer_1 (
    .in0(not_5_out), .in1(nand_1_out), .in2(nor_1_out), .in3(1'b0), .in4(not_6_out), .in5(not_1_out),
    .in6(xor_1_out), .in7(and_2_out), .in8(or_1_out), .in9(xnor_1_out), .in10(B1), .in11(and_1_out),
    .in12(1'b1), .in13(or_3_out), .in14(or_2_out), .in15(A1), .out(out_4), .sel(Selector));  // open: en
endmodule

module Alu_1bit_arithmati1 (
  input  [3:0] selector,
  input  A,
  input  B,
  output Sum,
  output Cout
);

  wire and_1_out, and_2_out, full_adder_usinghalg_1_carry, full_adder_usinghalg_1_sum,
       full_adder_usinghalg_2_carry, full_adder_usinghalg_2_sum, full_adder_usinghalg_3_carry,
       full_adder_usinghalg_3_sum, full_adder_usinghalg_4_carry, full_adder_usinghalg_4_sum,
       full_adder_usinghalg_5_carry, full_adder_usinghalg_5_sum, full_adder_usinghalg_6_carry,
       full_adder_usinghalg_6_sum, full_adder_usinghalg_7_carry, full_adder_usinghalg_7_sum,
       full_adder_usinghalg_8_carry, full_adder_usinghalg_8_sum, full_adder_usinghalg_9_carry,
       full_adder_usinghalg_9_sum, full_adder_usinghalg_10_carry, full_adder_usinghalg_10_sum,
       full_adder_usinghalg_11_carry, full_adder_usinghalg_11_sum, full_adder_usinghalg_12_carry,
       full_adder_usinghalg_12_sum, full_adder_usinghalg_13_carry, full_adder_usinghalg_13_sum,
       full_adder_usinghalg_14_carry, full_adder_usinghalg_14_sum, multiplier_1_cout, multiplier_1_out,
       not_1_out;

  not not_1 (not_1_out, B);
  full_adder_usingHalg full_adder_usinghalg_1 (
    .A(A), .B(1'b0), .Cin(1'b1), .sum(full_adder_usinghalg_1_sum), .carry(full_adder_usinghalg_1_carry));
  full_adder_usingHalg full_adder_usinghalg_2 (
    .A(A), .B(B), .Cin(1'b1), .sum(full_adder_usinghalg_2_sum), .carry(full_adder_usinghalg_2_carry));
  full_adder_usingHalg full_adder_usinghalg_3 (
    .A(A), .B(not_1_out), .Cin(1'b1), .sum(full_adder_usinghalg_3_sum), .carry(full_adder_usinghalg_3_carry));
  and and_1 (and_1_out, A, not_1_out);
  and and_2 (and_2_out, A, B);
  full_adder_usingHalg full_adder_usinghalg_4 (
    .A(and_1_out), .B(A), .Cin(1'b0), .sum(full_adder_usinghalg_4_sum), .carry(full_adder_usinghalg_4_carry));
  full_adder_usingHalg full_adder_usinghalg_5 (
    .A(and_1_out), .B(A), .Cin(B), .sum(full_adder_usinghalg_5_sum), .carry(full_adder_usinghalg_5_carry));
  full_adder_usingHalg full_adder_usinghalg_6 (
    .A(A), .B(B), .Cin(1'b1), .sum(full_adder_usinghalg_6_sum), .carry(full_adder_usinghalg_6_carry));
  full_adder_usingHalg full_adder_usinghalg_7 (
    .A(A), .B(and_2_out), .Cin(1'b0), .sum(full_adder_usinghalg_7_sum), .carry(full_adder_usinghalg_7_carry));
  full_adder_usingHalg full_adder_usinghalg_8 (
    .A(and_2_out), .B(1'b0), .Cin(1'b1), .sum(full_adder_usinghalg_8_sum),
    .carry(full_adder_usinghalg_8_carry));
  full_adder_usingHalg full_adder_usinghalg_9 (
    .A(A), .B(B), .Cin(1'b0), .sum(full_adder_usinghalg_9_sum), .carry(full_adder_usinghalg_9_carry));
  full_adder_usingHalg full_adder_usinghalg_10 (
    .A(and_2_out), .B(A), .Cin(not_1_out), .sum(full_adder_usinghalg_10_sum),
    .carry(full_adder_usinghalg_10_carry));
  full_adder_usingHalg full_adder_usinghalg_11 (
    .A(and_2_out), .B(1'b1), .Cin(1'b0), .sum(full_adder_usinghalg_11_sum),
    .carry(full_adder_usinghalg_11_carry));
  full_adder_usingHalg full_adder_usinghalg_12 (
    .A(A), .B(A), .Cin(1'b0), .sum(full_adder_usinghalg_12_sum), .carry(full_adder_usinghalg_12_carry));
  full_adder_usingHalg full_adder_usinghalg_13 (
    .A(A), .B(B), .Cin(A), .sum(full_adder_usinghalg_13_sum), .carry(full_adder_usinghalg_13_carry));
  full_adder_usingHalg full_adder_usinghalg_14 (
    .A(A), .B(not_1_out), .Cin(A), .sum(full_adder_usinghalg_14_sum), .carry(full_adder_usinghalg_14_carry));
  Multiplier #(.width(1)) multiplier_1 (.a(A), .b(B), .out(multiplier_1_out), .cin(1'b0), .cout(multiplier_1_cout));
  Multiplexer #(.select(4)) multiplexer_1 (
    .in0(full_adder_usinghalg_1_sum), .in1(full_adder_usinghalg_2_sum), .in2(full_adder_usinghalg_3_sum),
    .in3(1'b1), .in4(full_adder_usinghalg_4_sum), .in5(full_adder_usinghalg_5_sum),
    .in6(full_adder_usinghalg_6_sum), .in7(full_adder_usinghalg_8_sum), .in8(full_adder_usinghalg_7_sum),
    .in9(full_adder_usinghalg_9_sum), .in10(full_adder_usinghalg_10_sum), .in11(full_adder_usinghalg_11_sum),
    .in12(full_adder_usinghalg_12_sum), .in13(full_adder_usinghalg_13_sum),
    .in14(full_adder_usinghalg_14_sum), .in15(multiplier_1_out), .out(Sum), .sel(selector));  // open: en
  Multiplexer #(.select(4)) multiplexer_2 (
    .in0(full_adder_usinghalg_1_carry), .in1(full_adder_usinghalg_2_carry),
    .in2(full_adder_usinghalg_3_carry), .in3(1'b0), .in4(full_adder_usinghalg_4_carry),
    .in5(full_adder_usinghalg_5_carry), .in6(full_adder_usinghalg_6_carry),
    .in7(full_adder_usinghalg_8_carry), .in8(full_adder_usinghalg_7_carry),
    .in9(full_adder_usinghalg_9_carry), .in10(full_adder_usinghalg_10_carry),
    .in11(full_adder_usinghalg_11_carry), .in12(full_adder_usinghalg_12_carry),
    .in13(full_adder_usinghalg_13_carry), .in14(full_adder_usinghalg_14_carry), .in15(multiplier_1_cout),
    .out(Cout), .sel(selector));  // open: en
endmodule

module Alu_1bit_arithmatic2 (
  input  [3:0] selector,
  input  A,
  input  B,
  output res,
  output Carry
);

  wire and_1_out, and_2_out, full_adder_usinghalg_1_carry, full_adder_usinghalg_1_sum,
       full_adder_usinghalg_2_carry, full_adder_usinghalg_2_sum, full_adder_usinghalg_3_carry,
       full_adder_usinghalg_3_sum, full_adder_usinghalg_4_carry, full_adder_usinghalg_4_sum,
       full_adder_usinghalg_5_carry, full_adder_usinghalg_5_sum, full_adder_usinghalg_6_carry,
       full_adder_usinghalg_6_sum, full_subtractor_1_bout, full_subtractor_1_d, full_subtractor_2_bout,
       full_subtractor_2_d, full_subtractor_3_bout, full_subtractor_3_d, full_subtractor_4_bout,
       full_subtractor_4_d, full_subtractor_5_bout, full_subtractor_5_d, full_subtractor_6_bout,
       full_subtractor_6_d, full_subtractor_7_bout, full_subtractor_7_d, full_subtractor_8_bout,
       full_subtractor_8_d, full_subtractor_9_bout, full_subtractor_9_d, full_subtractor_10_bout,
       full_subtractor_10_d, full_subtractor_11_bout, full_subtractor_11_d, full_subtractor_12_bout,
       full_subtractor_12_d, full_subtractor_13_bout, full_subtractor_13_d, halg_subtractor_1_bow,
       halg_subtractor_1_d, multiplier_1_cout, multiplier_1_out, not_1_out;

  not not_1 (not_1_out, B);
  full_adder_usingHalg full_adder_usinghalg_1 (
    .A(A), .B(B), .Cin(1'b0), .sum(full_adder_usinghalg_1_sum), .carry(full_adder_usinghalg_1_carry));
  full_adder_usingHalg full_adder_usinghalg_2 (
    .A(not_1_out), .B(A), .Cin(1'b0), .sum(full_adder_usinghalg_2_sum), .carry(full_adder_usinghalg_2_carry));
  and and_1 (and_1_out, A, not_1_out);
  full_adder_usingHalg full_adder_usinghalg_3 (
    .A(A), .B(B), .Cin(1'b0), .sum(full_adder_usinghalg_3_sum), .carry(full_adder_usinghalg_3_carry));
  and and_2 (and_2_out, A, B);
  full_adder_usingHalg full_adder_usinghalg_4 (
    .A(A), .B(not_1_out), .Cin(1'b0), .sum(full_adder_usinghalg_4_sum), .carry(full_adder_usinghalg_4_carry));
  full_adder_usingHalg full_adder_usinghalg_5 (
    .A(A), .B(B), .Cin(1'b0), .sum(full_adder_usinghalg_5_sum), .carry(full_adder_usinghalg_5_carry));
  full_adder_usingHalg full_adder_usinghalg_6 (
    .A(A), .B(not_1_out), .Cin(1'b0), .sum(full_adder_usinghalg_6_sum), .carry(full_adder_usinghalg_6_carry));
  halg_subtractor halg_subtractor_1 (.D(halg_subtractor_1_d), .Bow(halg_subtractor_1_bow), .B(1'b1), .A(A));
  full_subtractor full_subtractor_1 (
    .D(full_subtractor_1_d), .Bout(full_subtractor_1_bout), .Bin(1'b1), .A(full_adder_usinghalg_1_sum),
    .B(full_adder_usinghalg_1_carry));
  full_subtractor full_subtractor_2 (
    .D(full_subtractor_2_d), .Bout(full_subtractor_2_bout), .Bin(1'b1), .A(full_adder_usinghalg_2_sum),
    .B(full_adder_usinghalg_2_carry));
  full_subtractor full_subtractor_3 (
    .D(full_subtractor_3_d), .Bout(full_subtractor_3_bout), .Bin(1'b0), .A(A), .B(and_1_out));
  full_subtractor full_subtractor_4 (
    .D(full_subtractor_4_d), .Bout(full_subtractor_4_bout), .Bin(and_1_out), .A(full_adder_usinghalg_3_sum),
    .B(full_adder_usinghalg_3_carry));
  full_subtractor full_subtractor_5 (.D(full_subtractor_5_d), .Bout(full_subtractor_5_bout), .Bin(1'b1), .A(A), .B(B));
  full_subtractor full_subtractor_6 (
    .D(full_subtractor_6_d), .Bout(full_subtractor_6_bout), .Bin(1'b0), .A(and_2_out), .B(1'b1));
  full_subtractor full_subtractor_7 (
    .D(full_subtractor_7_d), .Bout(full_subtractor_7_bout), .Bin(1'b0), .A(A), .B(and_2_out));
  full_subtractor full_subtractor_8 (.D(full_subtractor_8_d), .Bout(full_subtractor_8_bout), .Bin(1'b0), .A(A), .B(B));
  full_subtractor full_subtractor_9 (
    .D(full_subtractor_9_d), .Bout(full_subtractor_9_bout), .Bin(and_2_out), .A(full_adder_usinghalg_4_sum),
    .B(full_adder_usinghalg_4_carry));
  full_subtractor full_subtractor_10 (
    .D(full_subtractor_10_d), .Bout(full_subtractor_10_bout), .Bin(1'b0), .A(and_2_out), .B(1'b1));
  full_subtractor full_subtractor_11 (
    .D(full_subtractor_11_d), .Bout(full_subtractor_11_bout), .Bin(1'b0), .A(A), .B(A));
  full_subtractor full_subtractor_12 (
    .D(full_subtractor_12_d), .Bout(full_subtractor_12_bout), .Bin(A), .A(full_adder_usinghalg_5_sum),
    .B(full_adder_usinghalg_5_carry));
  full_subtractor full_subtractor_13 (
    .D(full_subtractor_13_d), .Bout(full_subtractor_13_bout), .Bin(A), .A(full_adder_usinghalg_6_sum),
    .B(full_adder_usinghalg_6_carry));
  Multiplier #(.width(1)) multiplier_1 (.a(A), .b(B), .out(multiplier_1_out), .cin(1'b0), .cout(multiplier_1_cout));
  Multiplexer #(.select(4)) multiplexer_1 (
    .in0(halg_subtractor_1_d), .in1(full_subtractor_1_d), .in2(full_subtractor_2_d), .in3(1'b0),
    .in4(full_subtractor_3_d), .in5(full_subtractor_4_d), .in6(full_subtractor_5_d),
    .in7(full_subtractor_6_d), .in8(full_subtractor_7_d), .in9(full_subtractor_8_d),
    .in10(full_subtractor_9_d), .in11(full_subtractor_10_d), .in12(full_subtractor_11_d),
    .in13(full_subtractor_12_d), .in14(full_subtractor_13_d), .in15(multiplier_1_out), .out(res),
    .sel(selector));  // open: en
  Multiplexer #(.select(4)) multiplexer_2 (
    .in0(halg_subtractor_1_bow), .in1(full_subtractor_1_bout), .in2(full_subtractor_2_bout), .in3(1'b1),
    .in4(full_subtractor_3_bout), .in5(full_subtractor_4_bout), .in6(full_subtractor_5_bout),
    .in7(full_subtractor_6_bout), .in8(full_subtractor_7_bout), .in9(full_subtractor_8_bout),
    .in10(full_subtractor_9_bout), .in11(full_subtractor_10_bout), .in12(full_subtractor_11_bout),
    .in13(full_subtractor_12_bout), .in14(full_subtractor_13_bout), .in15(multiplier_1_cout), .out(Carry),
    .sel(selector));  // open: en
endmodule

module Alu_1bit_arithmatic (
  input  [3:0] Selector,
  input  Cin,
  input  A,
  input  B,
  output Cout,
  output Sum
);

  wire alu_1bit_arithmati1_1_cout, alu_1bit_arithmati1_1_sum, alu_1bit_arithmatic2_1_carry,
       alu_1bit_arithmatic2_1_res;

  Alu_1bit_arithmati1 alu_1bit_arithmati1_1 (
    .A(A), .B(B), .Sum(alu_1bit_arithmati1_1_sum), .Cout(alu_1bit_arithmati1_1_cout), .selector(Selector));
  Alu_1bit_arithmatic2 alu_1bit_arithmatic2_1 (
    .res(alu_1bit_arithmatic2_1_res), .Carry(alu_1bit_arithmatic2_1_carry), .A(A), .B(B), .selector(Selector));
  Multiplexer multiplexer_1 (
    .in0(alu_1bit_arithmati1_1_cout), .in1(alu_1bit_arithmatic2_1_carry), .out(Cout), .sel(Cin));  // open: en
  Multiplexer multiplexer_2 (
    .in0(alu_1bit_arithmati1_1_sum), .in1(alu_1bit_arithmatic2_1_res), .out(Sum), .sel(Cin));  // open: en
endmodule

module Alu_1bit (
  input  [3:0] Selector,
  input  Cin,
  input  M,
  input  A0,
  input  B0,
  output OUt,
  output Carry
);

  wire alu_1bit_arithmatic_1_sum, alu_1bit_logic_1_out_4;

  Alu_1bit_arithmatic alu_1bit_arithmatic_1 (
    .A(A0), .B(B0), .Selector(Selector), .Cin(Cin), .Cout(Carry), .Sum(alu_1bit_arithmatic_1_sum));
  Alu_1bit_logic alu_1bit_logic_1 (.A1(A0), .B1(B0), .Selector(Selector), .out_4(alu_1bit_logic_1_out_4));
  Multiplexer multiplexer_1 (
    .in0(alu_1bit_logic_1_out_4), .in1(alu_1bit_arithmatic_1_sum), .out(OUt), .sel(M));  // open: en
endmodule
